# Fritzing sketch MetroVariantTest (saved by Fritzing 0.9.9b)
breadboards: 1

parts:
  Part1 = Adafruit Metro M0 Express
  Part3 = Adafruit FTDI Friend [part_number="Adafruit #284"]
  Part4 = Adafruit FTDI Friend [part_number="Adafruit #284"]
  Part5 = Adafruit FTDI Friend [part_number="Adafruit #284"]
  ZS-042_RTC1 = ZS-042 RTC Module
  Part6 = INA219 High Side DC Current Sensor Breakout [part_number=904]

nets:
  N1: Part1.SCL, ZS-042_RTC1.SCL
  N2: Part1.SDA, ZS-042_RTC1.SDA
  GND: Part1.GND, Part3.GND, Part4.GND, Part5.GND, ZS-042_RTC1.GND, Part6.GND
  N3: Part1.D13, Part3.TX
  N4: Part1.D11, Part3.RX
  N5: Part1.D7, Part4.TX
  N6: Part1.D6, Part4.RX
  N7: Part1.D4, Part6.SDA
  N8: Part1.D3, Part6.SCL
  N9: Part1.D1, Part5.RX
  N10: Part1.D0, Part5.TX
  VCC: Part1.3.3V, ZS-042_RTC1.VCC, Part6.VCC

notes:
  Serial0 uses pins D11(TxD) and D13(RxD)
  Serial1 uses pins D1(TxD) and D0(RxD)
  Serial2 uses pins D6(TxD) and D7(RxD)
  Wire uses pins SCL and SDA
  Wire1 uses pins D4(SDA) and D3(SCL)
  Serial0
  Serial1
  Serial2
  Wire
  Wire1

custom parts:
  Adafruit Metro M0 Express: Metro is our series of microcontroller boards for use with the Arduino IDE. This new Metro board looks a whole lot like our original Metro 328, but with a huge upgrade. Instead of the ATmega328, this Metro features a ATSAMD21G18 chip, an ARM Cortex M0+. It's our first Metro that is designed for use with CircuitPython! CircuitPython is our beginner-oriented flavor of MicroPython - and as the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
  Adafruit FTDI Friend: Long gone are the days of parallel ports and serial ports. Now the USB port reigns supreme! But USB is hard, and you just want to transfer your every-day serial data from a microcontroller to computer. What now? Enter the FTDI Friend! The FTDI Friend is a tweaked out FTDI FT232RL chip adapter. Sure, like the well-known FTDI cable, it can provide power to your project and there are 4 signal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
  INA219 High Side DC Current Sensor Breakout: This breakout board will solve all your power-monitoring problems. Instead of struggling with two multimeters, you can just use the handy INA219B chip on this breakout to both measure both the high side voltage and DC current draw over I2C with 1% precision. Most current-measuring devices such as our current panel meter are only good for low side measuring. That means that unless you want to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
